# Fritzing sketch schematic (saved by Fritzing 0.9.6b)
breadboards: 1

parts:
  R1 = 2,2k Resistor [package=THT]
  Part1 = Arduino Uno (Rev3)
  R14 = Resistor [tolerance=±5% resistance=220 power=0.25 package=THT]
  co2_Solenoid_R15 = 2,2k Resistor [package=THT]
  R16 = 2,2k Resistor [package=THT]
  R17 = 2,2k Resistor [package=THT]
  R18 = 2,2k Resistor [package=THT]
  R19 = 2,2k Resistor [package=THT]
  R20 = 2,2k Resistor [package=THT]
  R21 = 2,2k Resistor [package=THT]
  R22 = 2,2k Resistor [package=THT]
  pin_7_fill_sol_3 = TRANSISTOR_NPN [part_number="MOSFET N-Channel 49A 55v" package=to-92-ammo]
  pin_6_fill_sol_2 = TRANSISTOR_NPN [part_number="MOSFET N-Channel 49A 55v" package=to-92-ammo]
  pin_5_fill_sol_1 = TRANSISTOR_NPN [part_number="MOSFET N-Channel 49A 55v" package=to-92-ammo]
  pin_4_fill_sol_co2 = TRANSISTOR_NPN [part_number="MOSFET N-Channel 49A 55v" package=to-92-ammo]
  pin_3_fill_tube_lift_sol = TRANSISTOR_NPN [part_number="MOSFET N-Channel 49A 55v" package=to-92-ammo]
  pin_2_canpush_Sol = TRANSISTOR_NPN [part_number="MOSFET N-Channel 49A 55v" package=to-92-ammo]
  D1 = Schottky Diode [part_number=1N5817 package="Melf DO-213 AB [SMD]"]
  pin_4_co2_solenoid = Terminal 2pin
  D2 = Schottky Diode [part_number=1N5817 package="Melf DO-213 AB [SMD]"]
  pin_3_fill_tube_lift_solenoid = Terminal 2pin
  D3 = Schottky Diode [part_number=1N5817 package="Melf DO-213 AB [SMD]"]
  pin_2_canpush_solenoid = Terminal 2pin
  D4 = Schottky Diode [part_number=1N5817 package="Melf DO-213 AB [SMD]"]
  pin_5_fill_solenoid_1 = Terminal 2pin
  D5 = Schottky Diode [part_number=1N5817 package="Melf DO-213 AB [SMD]"]
  pin_7_fill_solenoid_3 = Terminal 2pin
  D6 = Schottky Diode [part_number=1N5817 package="Melf DO-213 AB [SMD]"]
  pin_6_fill_solenoid_2 = Terminal 2pin
  R23 = Rotary Potentiometer (Small) [maximum_resistance=100kΩ package=THT]
  Beer_Fill_Sensor_2 = Terminal 2pin
  Beer_Fill_Sensor_3 = Terminal 2pin
  pin_8_Start_button = Terminal 2pin
  Beer_Fill_Sensor_1 = Terminal 2pin

nets:
  N1: R1.Pin_0, pin_3_fill_tube_lift_sol.E
  N2: Part1.A0, Beer_Fill_Sensor_1.pin_2
  N3: Part1.A1, Beer_Fill_Sensor_2.pin_2
  N4: Part1.A2, R20.Pin_0, Beer_Fill_Sensor_3.pin_1
  N5: Part1.A3, R23.wiper
  N6: Part1.D8, R14.Pin_1, pin_8_Start_button.pin_2
  N7: Part1.5V, pin_4_co2_solenoid.pin_1, D2.cathode, pin_3_fill_tube_lift_solenoid.pin_1, D3.cathode, pin_2_canpush_solenoid.pin_1, D4.cathode, pin_5_fill_solenoid_1.pin_1, D5.cathode, pin_7_fill_solenoid_3.pin_1, D6.cathode, pin_6_fill_solenoid_2.pin_1, R23.leg2, Beer_Fill_Sensor_2.pin_1, Beer_Fill_Sensor_3.pin_2, pin_8_Start_button.pin_1, Beer_Fill_Sensor_1.pin_1
  N8: Part1.GND, R14.Pin_0, R21.Pin_0, R22.Pin_0, pin_7_fill_sol_3.C, pin_6_fill_sol_2.B, pin_5_fill_sol_1.C, pin_4_fill_sol_co2.C, pin_3_fill_tube_lift_sol.C, pin_2_canpush_Sol.C, D6.anode, pin_6_fill_solenoid_2.pin_2, R23.leg1
  N9: co2_Solenoid_R15.Pin_0, pin_4_fill_sol_co2.E
  N10: R16.Pin_0, pin_5_fill_sol_1.E
  N11: R17.Pin_0, pin_6_fill_sol_2.E
  N12: R18.Pin_0, pin_7_fill_sol_3.E
  N13: R19.Pin_0, pin_2_canpush_Sol.E
  N14: pin_7_fill_sol_3.B, D5.anode, pin_7_fill_solenoid_3.pin_2
  N15: pin_5_fill_sol_1.B, D4.anode, pin_5_fill_solenoid_1.pin_2
  N16: pin_4_fill_sol_co2.B, D1.anode, pin_4_co2_solenoid.pin_2
  N17: pin_3_fill_tube_lift_sol.B, D2.anode, pin_3_fill_tube_lift_solenoid.pin_2
  N18: pin_2_canpush_Sol.B, D3.anode, pin_2_canpush_solenoid.pin_2

custom parts:
  2,2k Resistor: A generic resistor (0.25W)
  Terminal 2pin: 2-pin Terminal Block

// code stored in the sketch: OpenBeerFiller.ino
/**
 * Open Beer Filler
 * Copyright (c) 2020 Gerhard Potgieter [https://gerhardpotgieter.com]
 *
 * Based on an idea by Christopher Harrison-Hawkes [https://harrisonsbrewery.com]
 *
 * This program is free software: you can redistribute it and/or modify
 * it under the terms of the GNU General Public License as published by
 * the Free Software Foundation, either version 3 of the License, or
 * (at your option) any later version.
 *
 * This program is distributed in the hope that it will be useful,
 * but WITHOUT ANY WARRANTY; without even the implied warranty of
 * MERCHANTABILITY or FITNESS FOR A PARTICULAR PURPOSE.  See the
 * GNU General Public License for more details.
 *
 * You should have received a copy of the GNU General Public License
 * along with this program.  If not, see <http://www.gnu.org/licenses/>.
 *
 */
#pragma once;

#include "Config.h";
#include "InputConfig.h";

#ifndef ICACHE_RAM_ATTR
#define ICACHE_RAM_ATTR     __attribute__((section(".iram.text")))
#endif

/**
 * ***************************************************************************
 * ******************************* VARIABLES *********************************
 * ***************************************************************************
 */
bool fillSensor1Triggered = false;
bool fillSensor2Triggered = false;
bool fillSensor3Triggered = false;
bool fillingInProgress = false;

void ICACHE_RAM_ATTR triggerFullFillSensor1();
void ICACHE_RAM_ATTR triggerFullFillSensor2();
void ICACHE_RAM_ATTR triggerFullFillSensor3();

/**
 * ***************************************************************************
 * ******************************** FUNCTIONS ********************************
 * ***************************************************************************
 */
void setupPins() {
  // Beer inlet solenoids
  pinMode(START_BUTTON, INPUT);
  pinMode(BEER_INLET_SOL_1, OUTPUT);
  pinMode(BEER_INLET_SOL_2, OUTPUT);
  pinMode(BEER_INLET_SOL_3, OUTPUT);

  // Other solenoids controlling various things.
  pinMode(CO2_PURGE_SOL, OUTPUT);
  pinMode(FILL_RAIL_SOL, OUTPUT);
  pinMode(BEER_BELT_SOL, OUTPUT);

  // Fill sensors.
  pinMode(BEER_FILL_SENSOR_1, INPUT);
  pinMode(BEER_FILL_SENSOR_2, INPUT);
  pinMode(BEER_FILL_SENSOR_3, INPUT);
}

/**
 * Use iterrupts to trigger when a fill sensor is triggered.
 */
void setupInterrupts() {
  // Fire these functions when bottles are full.
  attachInterrupt(digitalPinToInterrupt(BEER_FILL_SENSOR_1), triggerFullFillSensor1, RISING);
  attachInterrupt(digitalPinToInterrupt(BEER_FILL_SENSOR_2), triggerFullFillSensor2, RISING);
  attachInterrupt(digitalPinToInterrupt(BEER_FILL_SENSOR_3), triggerFullFillSensor3, RISING);
}

/**
 * Fired when fill sensor 1 is triggered as full.
 */
void triggerFullFillSensor1() {
  Serial.println( "Beer fill sensor 1 triggered" );
  // Close beer inlet solenoid.
  digitalWrite(BEER_INLET_SOL_1, LOW);
  fillSensor1Triggered = true;
}

/**
 * Fired when fill sensor 1 is triggered as full.
 */
void triggerFullFillSensor2() {
  Serial.println( "Beer fill sensor 2 triggered" );
  // Close beer inlet solenoid.
  digitalWrite(BEER_INLET_SOL_2, LOW);
  fillSensor2Triggered = true;
}

/**
 * Fired when fill sensor 1 is triggered as full.
 */
void triggerFullFillSensor3() {
  Serial.println( "Beer fill sensor 3 triggered" );
  // Close beer inlet solenoid.
  digitalWrite(BEER_INLET_SOL_3, LOW);
  fillSensor3Triggered = true;
}

/**
 * Return whether all fill sensors have been triggered or not.
 */
bool allFillSensorsTriggered() {
  return fillSensor1Triggered && fillSensor2Triggered && fillSensor3Triggered;
}

void resetFillSensorTriggers() {
  fillSensor1Triggered = fillSensor2Triggered = fillSensor3Triggered = fillingInProgress = false;
}

/**
 * Open all beer inlet solenoids.
 */
void openBeerInlets() {
  Serial.println( "Opening all beer inlets" );
  digitalWrite(BEER_INLET_SOL_1, HIGH);
  digitalWrite(BEER_INLET_SOL_2, HIGH);
  digitalWrite(BEER_INLET_SOL_3, HIGH);
  fillingInProgress = true;
}

/**
 * Open the CO2 purge solenoid, wait a while and then close it again.
 */
void purgeCO2( bool retract = false ) {
  Serial.println( "Purging CO2" );
  digitalWrite(CO2_PURGE_SOL, HIGH);
  if(!retract) {
    delay(CO2_PURGE_PERIOD);
  } else {
    delay(CO2_PURGE_RETRACTION_PERIOD);
  }
  digitalWrite(CO2_PURGE_SOL, LOW);
}

/**
 * Raise the fillter tubes out of the bottles.
 */
void raiseFillerTubes() {
  Serial.println("Raising filler tubes");
  digitalWrite(FILL_RAIL_SOL, HIGH);
  delay (CO2_PURGE_RETRACTION_DELAY); // We use CO2_PURGE_RETRACTION_DELAY here as we want to start purging with CO2 as the fill rail raises.
}

/**
 * Lower the filler tubes into the bottles.
 */
void lowerFillerTubes() {
  Serial.println("Lowering filler tubes");
  digitalWrite(FILL_RAIL_SOL, LOW);
  delay (FILLER_TUBE_MOVEMENT_DELAY);
  // We might need to add a delay here depending on how long it takes to fully lower the tubes.
}

/**
 * Move the beer belt, wait a while and then stop it again.
 */
void moveBeerBelt() {
  Serial.println( "Moving beer belt" );
  digitalWrite(BEER_BELT_SOL, HIGH);
  delay(MOVE_BEER_BELT_PERIOD);
  digitalWrite(BEER_BELT_SOL, LOW);
}

/**
 * Read if the filler tube sensors have been triggered.
 */
void readFillSensors() {
  if(digitalRead(BEER_FILL_SENSOR_1)) {
    fillSensor1Triggered = true;
    digitalWrite(BEER_INLET_SOL_1, LOW);
    Serial.println("Filler tube 1 closed");
  }
  if(digitalRead(BEER_FILL_SENSOR_2)) {
    fillSensor2Triggered = true;
    digitalWrite(BEER_INLET_SOL_2, LOW);
    Serial.println("Filler tube 2 closed");
  }
  if(digitalRead(BEER_FILL_SENSOR_3)) {
    fillSensor3Triggered = true;
    digitalWrite(BEER_INLET_SOL_3, LOW);
    Serial.println("Filler tube 3 closed");
  }
}

/**
 * Main setup routine.
 */
void setup() {
  Serial.begin(9600);
  setupPins();
  resetunit();
  //setupInterrupts();
  //raiseFillerTubes();
}
/**
* Reset the unit,
*/
void resetunit() {
digitalWrite(BEER_INLET_SOL_1, LOW);
digitalWrite(BEER_INLET_SOL_2, LOW);
digitalWrite(BEER_INLET_SOL_3, LOW);
digitalWrite(BEER_BELT_SOL, LOW);
digitalWrite(FILL_RAIL_SOL, HIGH);
digitalWrite(CO2_PURGE_SOL, LOW);
Serial.println("Reseting Unit");
delay(MOVE_BEER_BELT_PERIOD); // just for testing
}

/**
 * The main program loop, where all the magic comes togetger.
 */
void loop() {
  // What do we want to do when the program starts? We cannot just start pouring beer????
  // Start the process.
  while(digitalRead(START_BUTTON)==LOW) {  Serial.println( "Waiting For Start Button" ); } // Yout will need to prees the start button for every run.
  // Move items into the filling area 
   moveBeerBelt();
  // The program will get stopped in this while() loop as untill the start button is pressed.
  // Lets assume the belt has bottles and there are empty bottles underneath the filler tubes.
  if ( ! allFillSensorsTriggered() && ! fillingInProgress ) {
    lowerFillerTubes();
    purgeCO2();
    openBeerInlets();  
  }

  //Wait here for all Fill Sensors to be triggered once filling begins.
  while ( ! allFillSensorsTriggered() && fillingInProgress ) {
    readFillSensors();
  }
  
  // If we are done filling, rase filling tubes, move the beer belt for next batch and reset the triggers to start all over again.
  if ( allFillSensorsTriggered() && fillingInProgress ) {
    raiseFillerTubes();
    purgeCO2(true);
    resetFillSensorTriggers();
  }
}
